// Logisim project big_subsystem_0000.circ as structural Verilog
module blue_indexing_all_on (
  input  big_index_turn,
  input  W3,
  input  W2,
  input  H3,
  input  H2,
  output index_turn
);

  wire and_1_out, not_3_out, not_4_out;

  // NOT_Gate not_1 has open pins: in=W3, out=open
  // NOT_Gate not_2 has open pins: in=W2, out=open
  not not_3 (not_3_out, H3);
  not not_4 (not_4_out, H2);
  and and_1 (and_1_out, W3, W2, not_3_out, not_4_out);
  and and_2 (index_turn, big_index_turn, and_1_out);
endmodule

module blue_indexing_type_7 (
  input  big_index_turn,
  input  W3,
  input  W2,
  input  H3,
  input  H2,
  output index_turn
);

  wire and_1_out, not_2_out, not_3_out, not_4_out;

  // NOT_Gate not_1 has open pins: in=W3, out=open
  not not_2 (not_2_out, W2);
  not not_3 (not_3_out, H3);
  not not_4 (not_4_out, H2);
  and and_1 (and_1_out, W3, not_2_out, not_3_out, not_4_out);
  and and_2 (index_turn, big_index_turn, and_1_out);
endmodule

module blue_indexing_type_8 (
  input  big_index_turn,
  input  W3,
  input  W2,
  input  H3,
  input  H2,
  output index_turn
);

  wire and_1_out, not_3_out;

  // NOT_Gate not_1 has open pins: in=W3, out=open
  // NOT_Gate not_2 has open pins: in=W2, out=open
  not not_3 (not_3_out, H3);
  // NOT_Gate not_4 has open pins: in=H2, out=open
  and and_1 (and_1_out, W3, W2, not_3_out, H2);
  and and_2 (index_turn, big_index_turn, and_1_out);
endmodule

module blue_indexing_type_9 (
  input  big_index_turn,
  input  W3,
  input  W2,
  input  H3,
  input  H2,
  output index_turn
);

  wire and_1_out, not_4_out;

  // NOT_Gate not_1 has open pins: in=W3, out=open
  // NOT_Gate not_2 has open pins: in=W2, out=open
  // NOT_Gate not_3 has open pins: in=H3, out=open
  not not_4 (not_4_out, H2);
  and and_1 (and_1_out, W3, W2, H3, not_4_out);
  and and_2 (index_turn, big_index_turn, and_1_out);
endmodule

module purple_indexing_all_on (
  input  big_index_turn,
  input  W3,
  input  W2,
  input  H3,
  input  H2,
  output index_turn
);

  wire and_1_out, and_2_out, not_1_out, not_2_out, or_1_out, or_2_out;

  not not_1 (not_1_out, W3);
  not not_2 (not_2_out, W2);
  // NOT_Gate not_3 has open pins: in=H3, out=open
  // NOT_Gate not_4 has open pins: in=H2, out=open
  and and_1 (and_1_out, H3, H2);
  and and_2 (and_2_out, not_2_out, or_1_out);
  or or_1 (or_1_out, H2, H3);
  or or_2 (or_2_out, not_1_out, and_1_out, and_2_out);
  and and_3 (index_turn, big_index_turn, or_2_out);
endmodule

module kmap_type_7 (
  input  index_turn,
  input  W1,
  input  W0,
  input  H1,
  input  H0,
  output on_color,
  output off_color
);

  wire and_1_out, and_2_out, and_3_out, and_4_out, not_3_out, not_4_out, not_5_out, or_1_out;

  // NOT_Gate not_1 has open pins: in=W1, out=open
  // NOT_Gate not_2 has open pins: in=W0, out=open
  not not_3 (not_3_out, H1);
  not not_4 (not_4_out, H0);
  and and_1 (and_1_out, W1, W0);
  and and_2 (and_2_out, W1, not_3_out);
  and and_3 (and_3_out, W1, not_4_out);
  and and_4 (and_4_out, W0, not_3_out, not_4_out);
  or or_1 (or_1_out, and_1_out, and_2_out, and_3_out, and_4_out);
  not not_5 (not_5_out, or_1_out);
  and and_5 (on_color, index_turn, or_1_out);
  and and_6 (off_color, index_turn, not_5_out);
endmodule

module kmap_type_8 (
  input  index_turn,
  input  W1,
  input  W0,
  input  H1,
  input  H0,
  output on_color,
  output off_color
);

  wire not_3_out, not_5_out, or_1_out;

  // NOT_Gate not_1 has open pins: in=W1, out=open
  // NOT_Gate not_2 has open pins: in=W0, out=open
  not not_3 (not_3_out, H1);
  // NOT_Gate not_4 has open pins: in=H0, out=open
  or or_1 (or_1_out, not_3_out, W0, W1);
  not not_5 (not_5_out, or_1_out);
  and and_1 (on_color, index_turn, or_1_out);
  and and_2 (off_color, index_turn, not_5_out);
endmodule

module kmap_type_9 (
  input  index_turn,
  input  W1,
  input  W0,
  input  H1,
  input  H0,
  output on_color,
  output off_color
);

  wire and_1_out, and_2_out, not_3_out, not_4_out, not_5_out, or_1_out;

  // NOT_Gate not_1 has open pins: in=W1, out=open
  // NOT_Gate not_2 has open pins: in=W0, out=open
  not not_3 (not_3_out, H1);
  not not_4 (not_4_out, H0);
  and and_1 (and_1_out, W1, not_3_out);
  and and_2 (and_2_out, W1, W0, H1, not_4_out);
  or or_1 (or_1_out, and_1_out, and_2_out);
  not not_5 (not_5_out, or_1_out);
  and and_3 (on_color, index_turn, or_1_out);
  and and_4 (off_color, index_turn, not_5_out);
endmodule

module big_subsystem_0000 (
  input  W5,
  input  W4,
  input  H5,
  input  H4,
  input  W3,
  input  W2,
  input  H3,
  input  H2,
  input  W1,
  input  W0,
  input  H1,
  input  H0,
  output x1,
  output x2
);

  wire and_1_out, BLU_IDX_ALL_ON_index_turn, BLU_IDX_TYPE_7_index_turn, BLU_IDX_TYPE_8_index_turn,
       BLU_IDX_TYPE_9_index_turn, not_1_out, not_2_out, not_3_out, not_4_out, PUR_IDX_ALL_ON_index_turn,
       TYPE_7_off_color, TYPE_7_on_color, TYPE_8_off_color, TYPE_8_on_color, TYPE_9_off_color,
       TYPE_9_on_color;

  not not_1 (not_1_out, W5);
  not not_2 (not_2_out, W4);
  not not_3 (not_3_out, H5);
  not not_4 (not_4_out, H4);
  // NOT_Gate not_5 has open pins: in=W3, out=open
  // NOT_Gate not_6 has open pins: in=W2, out=open
  // NOT_Gate not_7 has open pins: in=H3, out=open
  // NOT_Gate not_8 has open pins: in=H2, out=open
  // NOT_Gate not_9 has open pins: in=W1, out=open
  // NOT_Gate not_10 has open pins: in=W0, out=open
  // NOT_Gate not_11 has open pins: in=H1, out=open
  // NOT_Gate not_12 has open pins: in=H0, out=open
  and and_1 (and_1_out, not_1_out, not_2_out, not_3_out, not_4_out);
  purple_indexing_all_on PUR_IDX_ALL_ON (
    .big_index_turn(and_1_out), .W3(W3), .W2(W2), .H3(H3), .H2(H2), .index_turn(PUR_IDX_ALL_ON_index_turn));
  blue_indexing_type_7 BLU_IDX_TYPE_7 (
    .big_index_turn(and_1_out), .W3(W3), .W2(W2), .H3(H3), .H2(H2), .index_turn(BLU_IDX_TYPE_7_index_turn));
  blue_indexing_type_8 BLU_IDX_TYPE_8 (
    .big_index_turn(and_1_out), .W3(W3), .W2(W2), .H3(H3), .H2(H2), .index_turn(BLU_IDX_TYPE_8_index_turn));
  blue_indexing_type_9 BLU_IDX_TYPE_9 (
    .big_index_turn(and_1_out), .W3(W3), .W2(W2), .H3(H3), .H2(H2), .index_turn(BLU_IDX_TYPE_9_index_turn));
  blue_indexing_all_on BLU_IDX_ALL_ON (
    .big_index_turn(and_1_out), .W3(W3), .W2(W2), .H3(H3), .H2(H2), .index_turn(BLU_IDX_ALL_ON_index_turn));
  kmap_type_7 TYPE_7 (
    .index_turn(BLU_IDX_TYPE_7_index_turn), .W1(W1), .W0(W0), .H1(H1), .H0(H0), .on_color(TYPE_7_on_color),
    .off_color(TYPE_7_off_color));
  kmap_type_8 TYPE_8 (
    .index_turn(BLU_IDX_TYPE_8_index_turn), .W1(W1), .W0(W0), .H1(H1), .H0(H0), .on_color(TYPE_8_on_color),
    .off_color(TYPE_8_off_color));
  kmap_type_9 TYPE_9 (
    .index_turn(BLU_IDX_TYPE_9_index_turn), .W1(W1), .W0(W0), .H1(H1), .H0(H0), .on_color(TYPE_9_on_color),
    .off_color(TYPE_9_off_color));
  or or_1 (x1, PUR_IDX_ALL_ON_index_turn, TYPE_7_off_color, TYPE_8_off_color, TYPE_9_off_color);
  or or_2 (x2, TYPE_7_on_color, TYPE_8_on_color, TYPE_9_on_color, BLU_IDX_ALL_ON_index_turn);
endmodule
