// Logisim project big_subsystem_0010.circ as structural Verilog
module big_subsystem_0010 (
  input  W5,
  input  W4,
  input  H5,
  input  H4,
  input  W3,
  input  W2,
  input  H3,
  input  H2,
  input  W1,
  input  W0,
  input  H1,
  input  H0,
  output x1
);

  wire and_1_out, not_1_out, not_2_out, not_4_out;

  not not_1 (not_1_out, W5);
  not not_2 (not_2_out, W4);
  // NOT_Gate not_3 has open pins: in=H5, out=open
  not not_4 (not_4_out, H4);
  // NOT_Gate not_5 has open pins: in=W3, out=open
  // NOT_Gate not_6 has open pins: in=W2, out=open
  // NOT_Gate not_7 has open pins: in=H3, out=open
  // NOT_Gate not_8 has open pins: in=H2, out=open
  // NOT_Gate not_9 has open pins: in=W1, out=open
  // NOT_Gate not_10 has open pins: in=W0, out=open
  // NOT_Gate not_11 has open pins: in=H1, out=open
  // NOT_Gate not_12 has open pins: in=H0, out=open
  and and_1 (and_1_out, not_1_out, not_2_out, H5, not_4_out);
  buf or_1 (x1, and_1_out);  // OR_Gate
endmodule
