// Logisim project big_subsystem_0100.circ as structural Verilog
module yellow_indexing_all_on (
  input  big_index_turn,
  input  W3,
  input  W2,
  input  H3,
  input  H2,
  output index_turn
);

  wire and_1_out, not_3_out, not_4_out;

  // NOT_Gate not_1 has open pins: in=W3, out=open
  // NOT_Gate not_2 has open pins: in=W2, out=open
  not not_3 (not_3_out, H3);
  not not_4 (not_4_out, H2);
  and and_1 (and_1_out, W3, W2, not_3_out, not_4_out);
  and and_2 (index_turn, big_index_turn, and_1_out);
endmodule

module yellow_indexing_type_1 (
  input  big_index_turn,
  input  W3,
  input  W2,
  input  H3,
  input  H2,
  output index_turn
);

  wire and_1_out, not_2_out, not_3_out, not_4_out;

  // NOT_Gate not_1 has open pins: in=W3, out=open
  not not_2 (not_2_out, W2);
  not not_3 (not_3_out, H3);
  not not_4 (not_4_out, H2);
  and and_1 (and_1_out, W3, not_2_out, not_3_out, not_4_out);
  and and_2 (index_turn, big_index_turn, and_1_out);
endmodule

module yellow_indexing_type_2 (
  input  big_index_turn,
  input  W3,
  input  W2,
  input  H3,
  input  H2,
  output index_turn
);

  wire and_1_out, not_3_out;

  // NOT_Gate not_1 has open pins: in=W3, out=open
  // NOT_Gate not_2 has open pins: in=W2, out=open
  not not_3 (not_3_out, H3);
  // NOT_Gate not_4 has open pins: in=H2, out=open
  and and_1 (and_1_out, W3, W2, not_3_out, H2);
  and and_2 (index_turn, big_index_turn, and_1_out);
endmodule

module yellow_indexing_sp_type_3 (
  input  big_index_turn,
  input  W3,
  input  W2,
  input  H3,
  input  H2,
  output index_turn
);

  wire and_1_out, not_2_out, not_3_out;

  // NOT_Gate not_1 has open pins: in=W3, out=open
  not not_2 (not_2_out, W2);
  not not_3 (not_3_out, H3);
  // NOT_Gate not_4 has open pins: in=H2, out=open
  and and_1 (and_1_out, W3, not_2_out, not_3_out, H2);
  and and_2 (index_turn, big_index_turn, and_1_out);
endmodule

module yellow_indexing_type_11 (
  input  big_index_turn,
  input  W3,
  input  W2,
  input  H3,
  input  H2,
  output index_turn
);

  wire and_1_out, not_4_out;

  // NOT_Gate not_1 has open pins: in=W3, out=open
  // NOT_Gate not_2 has open pins: in=W2, out=open
  // NOT_Gate not_3 has open pins: in=H3, out=open
  not not_4 (not_4_out, H2);
  and and_1 (and_1_out, W3, W2, H3, not_4_out);
  and and_2 (index_turn, big_index_turn, and_1_out);
endmodule

module green_indexing_type_2 (
  input  big_index_turn,
  input  W3,
  input  W2,
  input  H3,
  input  H2,
  output index_turn
);

  wire and_1_out, not_1_out, not_3_out, not_4_out;

  not not_1 (not_1_out, W3);
  // NOT_Gate not_2 has open pins: in=W2, out=open
  not not_3 (not_3_out, H3);
  not not_4 (not_4_out, H2);
  and and_1 (and_1_out, not_1_out, W2, not_3_out, not_4_out);
  and and_2 (index_turn, big_index_turn, and_1_out);
endmodule

module green_indexing_type_11 (
  input  big_index_turn,
  input  W3,
  input  W2,
  input  H3,
  input  H2,
  output index_turn
);

  wire and_1_out, not_1_out, not_3_out;

  not not_1 (not_1_out, W3);
  // NOT_Gate not_2 has open pins: in=W2, out=open
  not not_3 (not_3_out, H3);
  // NOT_Gate not_4 has open pins: in=H2, out=open
  and and_1 (and_1_out, not_1_out, W2, not_3_out, H2);
  and and_2 (index_turn, big_index_turn, and_1_out);
endmodule

module green_indexing_type_12 (
  input  big_index_turn,
  input  W3,
  input  W2,
  input  H3,
  input  H2,
  output index_turn
);

  wire and_1_out, not_2_out, not_4_out;

  // NOT_Gate not_1 has open pins: in=W3, out=open
  not not_2 (not_2_out, W2);
  // NOT_Gate not_3 has open pins: in=H3, out=open
  not not_4 (not_4_out, H2);
  and and_1 (and_1_out, W3, not_2_out, H3, not_4_out);
  and and_2 (index_turn, big_index_turn, and_1_out);
endmodule

module green_indexing_type_1 (
  input  big_index_turn,
  input  W3,
  input  W2,
  input  H3,
  input  H2,
  output index_turn
);

  wire and_1_out;

  // NOT_Gate not_1 has open pins: in=W3, out=open
  // NOT_Gate not_2 has open pins: in=W2, out=open
  // NOT_Gate not_3 has open pins: in=H3, out=open
  // NOT_Gate not_4 has open pins: in=H2, out=open
  and and_1 (and_1_out, W3, W2, H3, H2);
  and and_2 (index_turn, big_index_turn, and_1_out);
endmodule

module blue_indexing_type_13 (
  input  big_index_turn,
  input  W3,
  input  W2,
  input  H3,
  input  H2,
  output index_turn
);

  wire and_1_out, not_1_out, not_2_out;

  not not_1 (not_1_out, W3);
  not not_2 (not_2_out, W2);
  // NOT_Gate not_3 has open pins: in=H3, out=open
  // NOT_Gate not_4 has open pins: in=H2, out=open
  and and_1 (and_1_out, not_1_out, not_2_out, H3, H2);
  and and_2 (index_turn, big_index_turn, and_1_out);
endmodule

module blue_indexing_all_on (
  input  big_index_turn,
  input  W3,
  input  W2,
  input  H3,
  input  H2,
  output index_turn
);

  wire and_1_out, and_2_out, and_3_out, and_4_out, not_1_out, not_2_out, not_3_out, not_4_out, or_1_out;

  not not_1 (not_1_out, W3);
  not not_2 (not_2_out, W2);
  not not_3 (not_3_out, H3);
  not not_4 (not_4_out, H2);
  and and_1 (and_1_out, not_1_out, not_2_out, not_3_out);
  and and_2 (and_2_out, not_1_out, H3, not_4_out);
  and and_3 (and_3_out, not_1_out, W2, H3);
  and and_4 (and_4_out, W3, not_2_out, H3, H2);
  or or_1 (or_1_out, and_1_out, and_2_out, and_3_out, and_4_out);
  and and_5 (index_turn, big_index_turn, or_1_out);
endmodule

module kmap_type_1 (
  input  index_turn,
  input  W1,
  input  W0,
  input  H1,
  input  H0,
  output on_color,
  output off_color
);

  wire and_1_out, and_2_out, and_3_out, and_4_out, and_5_out, not_3_out, not_4_out, not_5_out, or_1_out;

  // NOT_Gate not_1 has open pins: in=W1, out=open
  // NOT_Gate not_2 has open pins: in=W0, out=open
  not not_3 (not_3_out, H1);
  not not_4 (not_4_out, H0);
  and and_1 (and_1_out, not_3_out, not_4_out);
  and and_2 (and_2_out, W0, not_3_out);
  and and_3 (and_3_out, W1, W0);
  and and_4 (and_4_out, W1, not_3_out);
  and and_5 (and_5_out, W1, not_4_out);
  or or_1 (or_1_out, and_1_out, and_2_out, and_3_out, and_4_out, and_5_out);
  not not_5 (not_5_out, or_1_out);
  and and_6 (on_color, index_turn, or_1_out);
  and and_7 (off_color, index_turn, not_5_out);
endmodule

module kmap_type_2 (
  input  index_turn,
  input  W1,
  input  W0,
  input  H1,
  input  H0,
  output on_color,
  output off_color
);

  wire and_1_out, not_3_out, not_4_out, not_5_out, or_1_out;

  // NOT_Gate not_1 has open pins: in=W1, out=open
  // NOT_Gate not_2 has open pins: in=W0, out=open
  not not_3 (not_3_out, H1);
  not not_4 (not_4_out, H0);
  and and_1 (and_1_out, W0, not_4_out);
  or or_1 (or_1_out, not_3_out, W1, and_1_out);
  not not_5 (not_5_out, or_1_out);
  and and_2 (on_color, index_turn, or_1_out);
  and and_3 (off_color, index_turn, not_5_out);
endmodule

module kmap_sp_type_3 (
  input  index_turn,
  input  W1,
  input  W0,
  input  H1,
  input  H0,
  output x2,
  output x4,
  output x3
);

  wire and_1_out, and_2_out, nor_1_out, not_1_out, not_2_out, not_3_out, not_4_out;

  not not_1 (not_1_out, W1);
  not not_2 (not_2_out, W0);
  not not_3 (not_3_out, H1);
  not not_4 (not_4_out, H0);
  and and_1 (and_1_out, not_1_out, not_2_out, H1, H0);
  and and_2 (and_2_out, W1, W0, not_3_out, not_4_out);
  nor nor_1 (nor_1_out, and_1_out, and_2_out);
  and and_3 (x2, index_turn, and_1_out);
  and and_4 (x4, index_turn, and_2_out);
  and and_5 (x3, index_turn, nor_1_out);
endmodule

module kmap_type_11 (
  input  index_turn,
  input  W1,
  input  W0,
  input  H1,
  input  H0,
  output on_color,
  output off_color
);

  wire and_1_out, and_2_out, not_3_out, not_4_out, not_5_out, or_1_out;

  // NOT_Gate not_1 has open pins: in=W1, out=open
  // NOT_Gate not_2 has open pins: in=W0, out=open
  not not_3 (not_3_out, H1);
  not not_4 (not_4_out, H0);
  and and_1 (and_1_out, W1, W0, not_3_out);
  or or_1 (or_1_out, and_1_out, and_2_out);
  and and_2 (and_2_out, W1, not_3_out, not_4_out);
  not not_5 (not_5_out, or_1_out);
  and and_3 (on_color, index_turn, or_1_out);
  and and_4 (off_color, index_turn, not_5_out);
endmodule

module kmap_type_12 (
  input  index_turn,
  input  W1,
  input  W0,
  input  H1,
  input  H0,
  output on_color,
  output off_color
);

  wire and_1_out, and_2_out, and_3_out, not_3_out, not_4_out, not_5_out, or_1_out;

  // NOT_Gate not_1 has open pins: in=W1, out=open
  // NOT_Gate not_2 has open pins: in=W0, out=open
  not not_3 (not_3_out, H1);
  not not_4 (not_4_out, H0);
  and and_1 (and_1_out, W1, not_3_out);
  and and_2 (and_2_out, W1, W0, not_4_out);
  and and_3 (and_3_out, W0, not_3_out, not_4_out);
  or or_1 (or_1_out, and_1_out, and_2_out, and_3_out);
  not not_5 (not_5_out, or_1_out);
  and and_4 (on_color, index_turn, or_1_out);
  and and_5 (off_color, index_turn, not_5_out);
endmodule

module kmap_type_13 (
  input  index_turn,
  input  W1,
  input  W0,
  input  H1,
  input  H0,
  output on_color,
  output off_color
);

  wire and_1_out, and_2_out, and_3_out, not_3_out, not_4_out, not_5_out, or_1_out;

  // NOT_Gate not_1 has open pins: in=W1, out=open
  // NOT_Gate not_2 has open pins: in=W0, out=open
  not not_3 (not_3_out, H1);
  not not_4 (not_4_out, H0);
  and and_1 (and_1_out, W0, not_3_out);
  and and_2 (and_2_out, W0, not_4_out);
  and and_3 (and_3_out, not_3_out, not_4_out);
  or or_1 (or_1_out, W1, and_1_out, and_2_out, and_3_out);
  not not_5 (not_5_out, or_1_out);
  and and_4 (on_color, index_turn, or_1_out);
  and and_5 (off_color, index_turn, not_5_out);
endmodule

module big_subsystem_0100 (
  input  W5,
  input  W4,
  input  H5,
  input  H4,
  input  W3,
  input  W2,
  input  H3,
  input  H2,
  input  W1,
  input  W0,
  input  H1,
  input  H0,
  output x4,
  output x3,
  output x2,
  output x1
);

  wire and_1_out, BLU_IDX_ALL_ON_index_turn, BLU_IDX_TYPE_13_index_turn, GRE_IDX_TYPE_1_index_turn,
       GRE_IDX_TYPE_2_index_turn, GRE_IDX_TYPE_11_index_turn, GRE_IDX_TYPE_12_index_turn, not_1_out,
       not_3_out, not_4_out, SP_TYPE_3_x2, SP_TYPE_3_x3, SP_TYPE_3_x4, TYPE_1_2_off_color, TYPE_1_2_on_color,
       TYPE_1_off_color, TYPE_1_on_color, TYPE_2_2_off_color, TYPE_2_2_on_color, TYPE_2_off_color,
       TYPE_2_on_color, TYPE_11_2_off_color, TYPE_11_2_on_color, TYPE_11_off_color, TYPE_11_on_color,
       TYPE_12_off_color, TYPE_12_on_color, TYPE_13_off_color, TYPE_13_on_color, YEL_IDX_ALL_ON_index_turn,
       YEL_IDX_SP_TYPE_3_index_turn, YEL_IDX_TYPE_1_index_turn, YEL_IDX_TYPE_2_index_turn,
       YEL_IDX_TYPE_11_index_turn;

  not not_1 (not_1_out, W5);
  // NOT_Gate not_2 has open pins: in=W4, out=open
  not not_3 (not_3_out, H5);
  not not_4 (not_4_out, H4);
  // NOT_Gate not_5 has open pins: in=W3, out=open
  // NOT_Gate not_6 has open pins: in=W2, out=open
  // NOT_Gate not_7 has open pins: in=H3, out=open
  // NOT_Gate not_8 has open pins: in=H2, out=open
  // NOT_Gate not_9 has open pins: in=W1, out=open
  // NOT_Gate not_10 has open pins: in=W0, out=open
  // NOT_Gate not_11 has open pins: in=H1, out=open
  // NOT_Gate not_12 has open pins: in=H0, out=open
  and and_1 (and_1_out, not_1_out, W4, not_3_out, not_4_out);
  yellow_indexing_all_on YEL_IDX_ALL_ON (
    .big_index_turn(and_1_out), .W3(W3), .W2(W2), .H3(H3), .H2(H2), .index_turn(YEL_IDX_ALL_ON_index_turn));
  yellow_indexing_type_1 YEL_IDX_TYPE_1 (
    .big_index_turn(and_1_out), .W3(W3), .W2(W2), .H3(H3), .H2(H2), .index_turn(YEL_IDX_TYPE_1_index_turn));
  yellow_indexing_type_2 YEL_IDX_TYPE_2 (
    .big_index_turn(and_1_out), .W3(W3), .W2(W2), .H3(H3), .H2(H2), .index_turn(YEL_IDX_TYPE_2_index_turn));
  yellow_indexing_sp_type_3 YEL_IDX_SP_TYPE_3 (
    .big_index_turn(and_1_out), .W3(W3), .W2(W2), .H3(H3), .H2(H2), .index_turn(YEL_IDX_SP_TYPE_3_index_turn));
  yellow_indexing_type_11 YEL_IDX_TYPE_11 (
    .big_index_turn(and_1_out), .W3(W3), .W2(W2), .H3(H3), .H2(H2), .index_turn(YEL_IDX_TYPE_11_index_turn));
  green_indexing_type_2 GRE_IDX_TYPE_2 (
    .big_index_turn(and_1_out), .W3(W3), .W2(W2), .H3(H3), .H2(H2), .index_turn(GRE_IDX_TYPE_2_index_turn));
  green_indexing_type_11 GRE_IDX_TYPE_11 (
    .big_index_turn(and_1_out), .W3(W3), .W2(W2), .H3(H3), .H2(H2), .index_turn(GRE_IDX_TYPE_11_index_turn));
  green_indexing_type_12 GRE_IDX_TYPE_12 (
    .big_index_turn(and_1_out), .W3(W3), .W2(W2), .H3(H3), .H2(H2), .index_turn(GRE_IDX_TYPE_12_index_turn));
  green_indexing_type_1 GRE_IDX_TYPE_1 (
    .big_index_turn(and_1_out), .W3(W3), .W2(W2), .H3(H3), .H2(H2), .index_turn(GRE_IDX_TYPE_1_index_turn));
  blue_indexing_type_13 BLU_IDX_TYPE_13 (
    .big_index_turn(and_1_out), .W3(W3), .W2(W2), .H3(H3), .H2(H2), .index_turn(BLU_IDX_TYPE_13_index_turn));
  blue_indexing_all_on BLU_IDX_ALL_ON (
    .big_index_turn(and_1_out), .W3(W3), .W2(W2), .H3(H3), .H2(H2), .index_turn(BLU_IDX_ALL_ON_index_turn));
  kmap_type_1 TYPE_1 (
    .index_turn(YEL_IDX_TYPE_1_index_turn), .W1(W1), .W0(W0), .H1(H1), .H0(H0), .on_color(TYPE_1_on_color),
    .off_color(TYPE_1_off_color));
  kmap_type_2 TYPE_2 (
    .index_turn(YEL_IDX_TYPE_2_index_turn), .W1(W1), .W0(W0), .H1(H1), .H0(H0), .on_color(TYPE_2_on_color),
    .off_color(TYPE_2_off_color));
  kmap_sp_type_3 SP_TYPE_3 (
    .index_turn(YEL_IDX_SP_TYPE_3_index_turn), .W1(W1), .W0(W0), .H1(H1), .H0(H0), .x2(SP_TYPE_3_x2),
    .x4(SP_TYPE_3_x4), .x3(SP_TYPE_3_x3));
  kmap_type_11 TYPE_11 (
    .index_turn(YEL_IDX_TYPE_11_index_turn), .W1(W1), .W0(W0), .H1(H1), .H0(H0), .on_color(TYPE_11_on_color),
    .off_color(TYPE_11_off_color));
  kmap_type_2 TYPE_2_2 (
    .index_turn(GRE_IDX_TYPE_2_index_turn), .W1(W1), .W0(W0), .H1(H1), .H0(H0), .on_color(TYPE_2_2_on_color),
    .off_color(TYPE_2_2_off_color));
  kmap_type_11 TYPE_11_2 (
    .index_turn(GRE_IDX_TYPE_11_index_turn), .W1(W1), .W0(W0), .H1(H1), .H0(H0),
    .on_color(TYPE_11_2_on_color), .off_color(TYPE_11_2_off_color));
  kmap_type_12 TYPE_12 (
    .index_turn(GRE_IDX_TYPE_12_index_turn), .W1(W1), .W0(W0), .H1(H1), .H0(H0), .on_color(TYPE_12_on_color),
    .off_color(TYPE_12_off_color));
  kmap_type_1 TYPE_1_2 (
    .index_turn(GRE_IDX_TYPE_1_index_turn), .W1(W1), .W0(W0), .H1(H1), .H0(H0), .on_color(TYPE_1_2_on_color),
    .off_color(TYPE_1_2_off_color));
  kmap_type_13 TYPE_13 (
    .index_turn(BLU_IDX_TYPE_13_index_turn), .W1(W1), .W0(W0), .H1(H1), .H0(H0), .on_color(TYPE_13_on_color),
    .off_color(TYPE_13_off_color));
  or or_1 (x4, YEL_IDX_ALL_ON_index_turn, TYPE_1_on_color, TYPE_2_on_color, TYPE_11_on_color, SP_TYPE_3_x4);
  or or_2 (x3, TYPE_1_off_color, TYPE_2_off_color, TYPE_11_off_color, TYPE_2_2_on_color, TYPE_11_2_on_color, TYPE_12_on_color, TYPE_1_2_on_color, SP_TYPE_3_x3);
  or or_3 (x2, TYPE_2_2_off_color, TYPE_11_2_off_color, TYPE_12_off_color, TYPE_1_2_off_color, TYPE_13_on_color, BLU_IDX_ALL_ON_index_turn, SP_TYPE_3_x2);
  buf or_4 (x1, TYPE_13_off_color);  // OR_Gate
endmodule
