// Logisim project big_subsystem_0110.circ as structural Verilog
module color_indexing_template (
  input  big_index_turn,
  input  W3,
  input  W2,
  input  H3,
  input  H2,
  output index_turn
);

  wire undriven;

  // NOT_Gate not_1 has open pins: in=W3, out=open
  // NOT_Gate not_2 has open pins: in=W2, out=open
  // NOT_Gate not_3 has open pins: in=H3, out=open
  // NOT_Gate not_4 has open pins: in=H2, out=open
  and and_1 (index_turn, big_index_turn, undriven);
endmodule

module kmap_template (
  input  index_turn,
  input  W1,
  input  W0,
  input  H1,
  input  H0,
  output on_color,
  output off_color
);

  wire not_5_out, undriven;

  // NOT_Gate not_1 has open pins: in=W1, out=open
  // NOT_Gate not_2 has open pins: in=W0, out=open
  // NOT_Gate not_3 has open pins: in=H1, out=open
  // NOT_Gate not_4 has open pins: in=H0, out=open
  not not_5 (not_5_out, undriven);
  and and_1 (on_color, index_turn, undriven);
  and and_2 (off_color, index_turn, not_5_out);
endmodule

module purple_indexing_all_on (
  input  big_index_turn,
  input  W3,
  input  W2,
  input  H3,
  input  H2,
  output index_turn
);

  wire not_1_out, not_2_out, or_1_out;

  not not_1 (not_1_out, W3);
  not not_2 (not_2_out, W2);
  // NOT_Gate not_3 has open pins: in=H3, out=open
  // NOT_Gate not_4 has open pins: in=H2, out=open
  or or_1 (or_1_out, not_1_out, H2, H3, not_2_out);
  and and_1 (index_turn, big_index_turn, or_1_out);
endmodule

module blue_indexing_type_15 (
  input  big_index_turn,
  input  W3,
  input  W2,
  input  H3,
  input  H2,
  output index_turn
);

  wire and_1_out, not_3_out, not_4_out;

  // NOT_Gate not_1 has open pins: in=W3, out=open
  // NOT_Gate not_2 has open pins: in=W2, out=open
  not not_3 (not_3_out, H3);
  not not_4 (not_4_out, H2);
  and and_1 (and_1_out, W3, W2, not_3_out, not_4_out);
  and and_2 (index_turn, big_index_turn, and_1_out);
endmodule

module kmap_type_15 (
  input  index_turn,
  input  W1,
  input  W0,
  input  H1,
  input  H0,
  output on_color,
  output off_color
);

  wire and_1_out, and_2_out, and_3_out, not_3_out, not_4_out, not_5_out, or_1_out;

  // NOT_Gate not_1 has open pins: in=W1, out=open
  // NOT_Gate not_2 has open pins: in=W0, out=open
  not not_3 (not_3_out, H1);
  not not_4 (not_4_out, H0);
  and and_1 (and_1_out, W1, W0);
  and and_2 (and_2_out, W1, not_3_out);
  and and_3 (and_3_out, W0, not_3_out, not_4_out);
  or or_1 (or_1_out, and_1_out, and_2_out, and_3_out);
  not not_5 (not_5_out, or_1_out);
  and and_4 (on_color, index_turn, or_1_out);
  and and_5 (off_color, index_turn, not_5_out);
endmodule

module big_subsystem_0110 (
  input  W5,
  input  W4,
  input  H5,
  input  H4,
  input  W3,
  input  W2,
  input  H3,
  input  H2,
  input  W1,
  input  W0,
  input  H1,
  input  H0,
  output x1,
  output x2
);

  wire and_1_out, BLU_IDX_TYPE_15_index_turn, not_1_out, not_4_out, PUR_IDX_ALL_ON_index_turn,
       TYPE_15_off_color, TYPE_15_on_color;

  not not_1 (not_1_out, W5);
  // NOT_Gate not_2 has open pins: in=W4, out=open
  // NOT_Gate not_3 has open pins: in=H5, out=open
  not not_4 (not_4_out, H4);
  // NOT_Gate not_5 has open pins: in=W3, out=open
  // NOT_Gate not_6 has open pins: in=W2, out=open
  // NOT_Gate not_7 has open pins: in=H3, out=open
  // NOT_Gate not_8 has open pins: in=H2, out=open
  // NOT_Gate not_9 has open pins: in=W1, out=open
  // NOT_Gate not_10 has open pins: in=W0, out=open
  // NOT_Gate not_11 has open pins: in=H1, out=open
  // NOT_Gate not_12 has open pins: in=H0, out=open
  and and_1 (and_1_out, not_1_out, W4, H5, not_4_out);
  purple_indexing_all_on PUR_IDX_ALL_ON (
    .big_index_turn(and_1_out), .W3(W3), .W2(W2), .H3(H3), .H2(H2), .index_turn(PUR_IDX_ALL_ON_index_turn));
  blue_indexing_type_15 BLU_IDX_TYPE_15 (
    .big_index_turn(and_1_out), .W3(W3), .W2(W2), .H3(H3), .H2(H2), .index_turn(BLU_IDX_TYPE_15_index_turn));
  kmap_type_15 TYPE_15 (
    .index_turn(BLU_IDX_TYPE_15_index_turn), .W1(W1), .W0(W0), .H1(H1), .H0(H0), .on_color(TYPE_15_on_color),
    .off_color(TYPE_15_off_color));
  or or_1 (x1, PUR_IDX_ALL_ON_index_turn, TYPE_15_off_color);
  buf or_2 (x2, TYPE_15_on_color);  // OR_Gate
endmodule
