// Logisim project big_subsystem_1000.circ as structural Verilog: 17 circuits, main circuit main_draft
// x4
module main_draft (
  input  W5,
  input  W1,
  input  W4,
  input  W3,
  input  W0,
  input  H5,
  input  W2,
  input  H1,
  input  H4,
  input  H3,
  input  H0,
  input  H2,
  output x5,
  output x4
);

  wire and_1_out, and_2_out, and_3_out, and_4_out, and_5_out, and_6_out, and_7_out, and_8_out, and_10_out,
       and_11_out, and_12_out, and_13_out, and_14_out, and_15_out, and_16_out, and_17_out, and_18_out,
       and_19_out, and_20_out, and_21_out, and_22_out, and_23_out, not_2_out, not_3_out, not_4_out,
       not_5_out, not_6_out, not_7_out, not_8_out, not_11_out, not_12_out, not_13_out, not_14_out, or_1_out,
       or_2_out, or_3_out, or_4_out, or_5_out;

  // NOT_Gate not_1 has open pins: in=W5, out=open
  not not_2 (not_2_out, W4);
  not not_3 (not_3_out, H5);
  not not_4 (not_4_out, H4);
  and and_1 (and_1_out, W5, not_2_out, not_3_out, not_4_out);
  not not_5 (not_5_out, W3);
  not not_6 (not_6_out, W2);
  not not_7 (not_7_out, H3);
  not not_8 (not_8_out, H2);
  and and_2 (and_2_out, not_5_out, W2, not_7_out, not_8_out);
  and and_3 (and_3_out, W3, W2, not_7_out);
  or or_1 (or_1_out, and_3_out, and_4_out);
  and and_4 (and_4_out, W3, not_7_out, not_8_out);
  and and_5 (and_5_out, W3, not_6_out, not_7_out, H2);
  and and_6 (and_6_out, W3, W2, H3, not_8_out);
  and and_7 (and_7_out, W3, not_6_out, H3, not_8_out);
  and and_8 (and_8_out, W3, W2, H3, H2);
  // AND_Gate and_9 is placed but not wired
  or or_2 (or_2_out, and_5_out, and_6_out);
  or or_3 (or_3_out, and_7_out, and_8_out);
  and and_10 (and_10_out, or_2_out, and_1_out);
  kmap_type_1 kmap_type_1_1 ();  // open: index_turn, W1, W0, H1, H0, on_color, off_color
  and and_11 (and_11_out, and_1_out, and_2_out);
  // NOT_Gate not_9 has open pins: in=W1, out=open
  // NOT_Gate not_10 has open pins: in=W0, out=open
  not not_11 (not_11_out, H1);
  not not_12 (not_12_out, H0);
  and and_12 (and_12_out, not_11_out, not_12_out);
  and and_13 (and_13_out, W0, not_11_out);
  and and_14 (and_14_out, W1, W0);
  and and_15 (and_15_out, W1, not_11_out);
  and and_16 (and_16_out, W1, not_12_out);
  or or_4 (or_4_out, not_11_out, W1, and_17_out);
  and and_17 (and_17_out, W0, not_12_out);
  and and_18 (and_18_out, W1, W0, not_11_out, not_12_out);
  or or_5 (or_5_out, and_12_out, and_13_out, and_14_out, and_15_out, and_16_out);
  and and_19 (and_19_out, and_11_out, or_5_out);
  and and_20 (and_20_out, or_4_out, and_10_out);
  not not_13 (not_13_out, or_4_out);
  and and_21 (and_21_out, or_3_out, and_18_out);
  not not_14 (not_14_out, and_18_out);
  or or_6 (x5, and_19_out, or_1_out, and_20_out, and_21_out);
  and and_22 (and_22_out, not_13_out, and_10_out);
  and and_23 (and_23_out, not_14_out, or_3_out);
  or or_7 (x4, and_22_out, and_23_out);
endmodule

module color_indexing_template (
  input  big_index_turn,
  input  W3,
  input  W2,
  input  H3,
  input  H2,
  output index_turn
);

  wire undriven;

  // NOT_Gate not_1 has open pins: in=W3, out=open
  // NOT_Gate not_2 has open pins: in=W2, out=open
  // NOT_Gate not_3 has open pins: in=H3, out=open
  // NOT_Gate not_4 has open pins: in=H2, out=open
  and and_1 (index_turn, big_index_turn, undriven);
endmodule

module kmap_template (
  input  index_turn,
  input  W1,
  input  W0,
  input  H1,
  input  H0,
  output on_color,
  output off_color
);

  wire not_5_out, undriven;

  // NOT_Gate not_1 has open pins: in=W1, out=open
  // NOT_Gate not_2 has open pins: in=W0, out=open
  // NOT_Gate not_3 has open pins: in=H1, out=open
  // NOT_Gate not_4 has open pins: in=H0, out=open
  not not_5 (not_5_out, undriven);
  and and_1 (on_color, index_turn, undriven);
  and and_2 (off_color, index_turn, not_5_out);
endmodule

module red_indexing_all_on (
  input  big_index_turn,
  input  W3,
  input  W2,
  input  H3,
  input  H2,
  output index_turn
);

  wire and_1_out, not_3_out, not_4_out, or_1_out;

  // NOT_Gate not_1 has open pins: in=W3, out=open
  // NOT_Gate not_2 has open pins: in=W2, out=open
  not not_3 (not_3_out, H3);
  not not_4 (not_4_out, H2);
  or or_1 (or_1_out, W2, not_4_out);
  and and_1 (and_1_out, W3, not_3_out, or_1_out);
  and and_2 (index_turn, big_index_turn, and_1_out);
endmodule

module red_indexing_type_1 (
  input  big_index_turn,
  input  W3,
  input  W2,
  input  H3,
  input  H2,
  output index_turn
);

  wire and_1_out, not_1_out, not_3_out, not_4_out;

  not not_1 (not_1_out, W3);
  // NOT_Gate not_2 has open pins: in=W2, out=open
  not not_3 (not_3_out, H3);
  not not_4 (not_4_out, H2);
  and and_1 (and_1_out, not_1_out, W2, not_3_out, not_4_out);
  and and_2 (index_turn, big_index_turn, and_1_out);
endmodule

module red_indexing_type_2 (
  input  big_index_turn,
  input  W3,
  input  W2,
  input  H3,
  input  H2,
  output index_turn
);

  wire and_1_out, and_2_out, not_2_out, not_3_out, not_4_out, or_1_out;

  // NOT_Gate not_1 has open pins: in=W3, out=open
  not not_2 (not_2_out, W2);
  not not_3 (not_3_out, H3);
  not not_4 (not_4_out, H2);
  and and_1 (and_1_out, W3, not_2_out, not_3_out, H2);
  or or_1 (or_1_out, and_1_out, and_2_out);
  and and_2 (and_2_out, W3, W2, H3, not_4_out);
  and and_3 (index_turn, big_index_turn, or_1_out);
endmodule

module red_indexing_type_3 (
  input  big_index_turn,
  input  W3,
  input  W2,
  input  H3,
  input  H2,
  output index_turn
);

  wire and_1_out, and_2_out, not_2_out, not_4_out, or_1_out;

  // NOT_Gate not_1 has open pins: in=W3, out=open
  not not_2 (not_2_out, W2);
  // NOT_Gate not_3 has open pins: in=H3, out=open
  not not_4 (not_4_out, H2);
  and and_1 (and_1_out, W3, W2, H3, H2);
  or or_1 (or_1_out, and_1_out, and_2_out);
  and and_2 (and_2_out, W3, not_2_out, H3, not_4_out);
  and and_3 (index_turn, big_index_turn, or_1_out);
endmodule

module yellow_indexing_all_on (
  input  big_index_turn,
  input  W3,
  input  W2,
  input  H3,
  input  H2,
  output index_turn
);

  wire and_1_out, and_2_out, and_3_out, and_4_out, not_1_out, not_2_out, not_3_out, or_1_out;

  not not_1 (not_1_out, W3);
  not not_2 (not_2_out, W2);
  not not_3 (not_3_out, H3);
  // NOT_Gate not_4 has open pins: in=H2, out=open
  and and_1 (and_1_out, not_1_out, not_2_out, not_3_out);
  and and_2 (and_2_out, not_1_out, not_3_out, H2);
  and and_3 (and_3_out, not_1_out, W2, H3);
  and and_4 (and_4_out, W3, not_2_out, H3, H2);
  or or_1 (or_1_out, and_1_out, and_2_out, and_3_out, and_4_out);
  and and_5 (index_turn, big_index_turn, or_1_out);
endmodule

module yellow_indexing_type_4 (
  input  big_index_turn,
  input  W3,
  input  W2,
  input  H3,
  input  H2,
  output index_turn
);

  wire and_1_out, not_1_out, not_2_out, not_4_out;

  not not_1 (not_1_out, W3);
  not not_2 (not_2_out, W2);
  // NOT_Gate not_3 has open pins: in=H3, out=open
  not not_4 (not_4_out, H2);
  and and_1 (and_1_out, not_1_out, not_2_out, H3, not_4_out);
  and and_2 (index_turn, big_index_turn, and_1_out);
endmodule

module yellow_indexing_type_5 (
  input  big_index_turn,
  input  W3,
  input  W2,
  input  H3,
  input  H2,
  output index_turn
);

  wire and_1_out, not_1_out, not_2_out;

  not not_1 (not_1_out, W3);
  not not_2 (not_2_out, W2);
  // NOT_Gate not_3 has open pins: in=H3, out=open
  // NOT_Gate not_4 has open pins: in=H2, out=open
  and and_1 (and_1_out, not_1_out, not_2_out, H3, H2);
  and and_2 (index_turn, big_index_turn, and_1_out);
endmodule

module kmap_type_1 (
  input  index_turn,
  input  W1,
  input  W0,
  input  H1,
  input  H0,
  output on_color,
  output off_color
);

  wire and_1_out, and_2_out, and_3_out, and_4_out, and_5_out, not_3_out, not_4_out, not_5_out, or_1_out;

  // NOT_Gate not_1 has open pins: in=W1, out=open
  // NOT_Gate not_2 has open pins: in=W0, out=open
  not not_3 (not_3_out, H1);
  not not_4 (not_4_out, H0);
  and and_1 (and_1_out, not_3_out, not_4_out);
  and and_2 (and_2_out, W0, not_3_out);
  and and_3 (and_3_out, W1, W0);
  and and_4 (and_4_out, W1, not_3_out);
  and and_5 (and_5_out, W1, not_4_out);
  or or_1 (or_1_out, and_1_out, and_2_out, and_3_out, and_4_out, and_5_out);
  not not_5 (not_5_out, or_1_out);
  and and_6 (on_color, index_turn, or_1_out);
  and and_7 (off_color, index_turn, not_5_out);
endmodule

module kmap_type_2 (
  input  index_turn,
  input  W1,
  input  W0,
  input  H1,
  input  H0,
  output on_color,
  output off_color
);

  wire and_1_out, not_3_out, not_4_out, not_5_out, or_1_out;

  // NOT_Gate not_1 has open pins: in=W1, out=open
  // NOT_Gate not_2 has open pins: in=W0, out=open
  not not_3 (not_3_out, H1);
  not not_4 (not_4_out, H0);
  and and_1 (and_1_out, W0, not_4_out);
  or or_1 (or_1_out, not_3_out, W1, and_1_out);
  not not_5 (not_5_out, or_1_out);
  and and_2 (on_color, index_turn, or_1_out);
  and and_3 (off_color, index_turn, not_5_out);
endmodule

module kmap_type_3 (
  input  index_turn,
  input  W1,
  input  W0,
  input  H1,
  input  H0,
  output on_color,
  output off_color
);

  wire and_1_out, not_3_out, not_4_out, not_5_out;

  // NOT_Gate not_1 has open pins: in=W1, out=open
  // NOT_Gate not_2 has open pins: in=W0, out=open
  not not_3 (not_3_out, H1);
  not not_4 (not_4_out, H0);
  and and_1 (and_1_out, W1, W0, not_3_out, not_4_out);
  not not_5 (not_5_out, and_1_out);
  and and_2 (on_color, index_turn, and_1_out);
  and and_3 (off_color, index_turn, not_5_out);
endmodule

module kmap_type_4 (
  input  index_turn,
  input  W1,
  input  W0,
  input  H1,
  input  H0,
  output on_color,
  output off_color
);

  wire not_3_out, not_4_out, not_5_out, or_1_out;

  // NOT_Gate not_1 has open pins: in=W1, out=open
  // NOT_Gate not_2 has open pins: in=W0, out=open
  not not_3 (not_3_out, H1);
  not not_4 (not_4_out, H0);
  or or_1 (or_1_out, W1, W0, not_3_out, not_4_out);
  not not_5 (not_5_out, or_1_out);
  and and_1 (on_color, index_turn, or_1_out);
  and and_2 (off_color, index_turn, not_5_out);
endmodule

module kmap_type_5 (
  input  index_turn,
  input  W1,
  input  W0,
  input  H1,
  input  H0,
  output on_color,
  output off_color
);

  wire and_1_out, and_2_out, and_3_out, not_3_out, not_4_out, not_5_out, or_1_out;

  // NOT_Gate not_1 has open pins: in=W1, out=open
  // NOT_Gate not_2 has open pins: in=W0, out=open
  not not_3 (not_3_out, H1);
  not not_4 (not_4_out, H0);
  and and_1 (and_1_out, W1, W0, not_3_out);
  and and_2 (and_2_out, W1, not_3_out, not_4_out);
  and and_3 (and_3_out, W1, W0, not_4_out);
  or or_1 (or_1_out, and_1_out, and_2_out, and_3_out);
  not not_5 (not_5_out, or_1_out);
  and and_4 (on_color, index_turn, or_1_out);
  and and_5 (off_color, index_turn, not_5_out);
endmodule

module big_subsystem_1000 (
  input  W5,
  input  W4,
  input  H5,
  input  H4,
  input  W3,
  input  W2,
  input  H3,
  input  H2,
  input  W1,
  input  W0,
  input  H1,
  input  H0,
  output x5,
  output x4,
  output x3
);

  wire and_1_out, not_2_out, not_3_out, not_4_out, RED_IDX_ALL_ON_index_turn, RED_IDX_TYPE_1_index_turn,
       RED_IDX_TYPE_2_index_turn, RED_IDX_TYPE_3_index_turn, TYPE_1_off_color, TYPE_1_on_color,
       TYPE_2_off_color, TYPE_2_on_color, TYPE_3_off_color, TYPE_3_on_color, TYPE_4_off_color,
       TYPE_4_on_color, TYPE_5_off_color, TYPE_5_on_color, YEL_IDX_ALL_ON_index_turn,
       YEL_IDX_TYPE_4_index_turn, YEL_IDX_TYPE_5_index_turn;

  // NOT_Gate not_1 has open pins: in=W5, out=open
  not not_2 (not_2_out, W4);
  not not_3 (not_3_out, H5);
  not not_4 (not_4_out, H4);
  // NOT_Gate not_5 has open pins: in=W3, out=open
  // NOT_Gate not_6 has open pins: in=W2, out=open
  // NOT_Gate not_7 has open pins: in=H3, out=open
  // NOT_Gate not_8 has open pins: in=H2, out=open
  // NOT_Gate not_9 has open pins: in=W1, out=open
  // NOT_Gate not_10 has open pins: in=W0, out=open
  // NOT_Gate not_11 has open pins: in=H1, out=open
  // NOT_Gate not_12 has open pins: in=H0, out=open
  and and_1 (and_1_out, W5, not_2_out, not_3_out, not_4_out);
  red_indexing_all_on RED_IDX_ALL_ON (
    .big_index_turn(and_1_out), .W3(W3), .W2(W2), .H3(H3), .H2(H2), .index_turn(RED_IDX_ALL_ON_index_turn));
  red_indexing_type_1 RED_IDX_TYPE_1 (
    .big_index_turn(and_1_out), .W3(W3), .W2(W2), .H3(H3), .H2(H2), .index_turn(RED_IDX_TYPE_1_index_turn));
  red_indexing_type_2 RED_IDX_TYPE_2 (
    .big_index_turn(and_1_out), .W3(W3), .W2(W2), .H3(H3), .H2(H2), .index_turn(RED_IDX_TYPE_2_index_turn));
  red_indexing_type_3 RED_IDX_TYPE_3 (
    .big_index_turn(and_1_out), .W3(W3), .W2(W2), .H3(H3), .H2(H2), .index_turn(RED_IDX_TYPE_3_index_turn));
  yellow_indexing_all_on YEL_IDX_ALL_ON (
    .big_index_turn(and_1_out), .W3(W3), .W2(W2), .H3(H3), .H2(H2), .index_turn(YEL_IDX_ALL_ON_index_turn));
  yellow_indexing_type_4 YEL_IDX_TYPE_4 (
    .big_index_turn(and_1_out), .W3(W3), .W2(W2), .H3(H3), .H2(H2), .index_turn(YEL_IDX_TYPE_4_index_turn));
  yellow_indexing_type_5 YEL_IDX_TYPE_5 (
    .big_index_turn(and_1_out), .W3(W3), .W2(W2), .H3(H3), .H2(H2), .index_turn(YEL_IDX_TYPE_5_index_turn));
  kmap_type_1 TYPE_1 (
    .index_turn(RED_IDX_TYPE_1_index_turn), .W1(W1), .W0(W0), .H1(H1), .H0(H0), .on_color(TYPE_1_on_color),
    .off_color(TYPE_1_off_color));
  kmap_type_2 TYPE_2 (
    .index_turn(RED_IDX_TYPE_2_index_turn), .W1(W1), .W0(W0), .H1(H1), .H0(H0), .on_color(TYPE_2_on_color),
    .off_color(TYPE_2_off_color));
  kmap_type_3 TYPE_3 (
    .index_turn(RED_IDX_TYPE_3_index_turn), .W1(W1), .W0(W0), .H1(H1), .H0(H0), .on_color(TYPE_3_on_color),
    .off_color(TYPE_3_off_color));
  kmap_type_4 TYPE_4 (
    .index_turn(YEL_IDX_TYPE_4_index_turn), .W1(W1), .W0(W0), .H1(H1), .H0(H0), .on_color(TYPE_4_on_color),
    .off_color(TYPE_4_off_color));
  kmap_type_5 TYPE_5 (
    .index_turn(YEL_IDX_TYPE_5_index_turn), .W1(W1), .W0(W0), .H1(H1), .H0(H0), .on_color(TYPE_5_on_color),
    .off_color(TYPE_5_off_color));
  or or_1 (x5, RED_IDX_ALL_ON_index_turn, TYPE_1_on_color, TYPE_2_on_color, TYPE_3_on_color);
  or or_2 (x4, TYPE_1_off_color, TYPE_2_off_color, TYPE_3_off_color, YEL_IDX_ALL_ON_index_turn, TYPE_4_on_color, TYPE_5_on_color);
  or or_3 (x3, TYPE_4_off_color, TYPE_5_off_color);
endmodule

module main (
  input  W5,
  input  W4,
  input  W3,
  input  W2,
  input  W1,
  input  W0,
  input  H5,
  input  H4,
  input  H3,
  input  H2,
  input  H1,
  input  H0
);
endmodule
