// Logisim project big_subsystem_1100.circ as structural Verilog
module color_indexing_template (
  input  big_index_turn,
  input  W3,
  input  W2,
  input  H3,
  input  H2,
  output index_turn
);

  wire undriven;

  // NOT_Gate not_1 has open pins: in=W3, out=open
  // NOT_Gate not_2 has open pins: in=W2, out=open
  // NOT_Gate not_3 has open pins: in=H3, out=open
  // NOT_Gate not_4 has open pins: in=H2, out=open
  and and_1 (index_turn, big_index_turn, undriven);
endmodule

module kmap_template (
  input  index_turn,
  input  W1,
  input  W0,
  input  H1,
  input  H0,
  output on_color,
  output off_color
);

  wire not_5_out, undriven;

  // NOT_Gate not_1 has open pins: in=W1, out=open
  // NOT_Gate not_2 has open pins: in=W0, out=open
  // NOT_Gate not_3 has open pins: in=H1, out=open
  // NOT_Gate not_4 has open pins: in=H0, out=open
  not not_5 (not_5_out, undriven);
  and and_1 (on_color, index_turn, undriven);
  and and_2 (off_color, index_turn, not_5_out);
endmodule

module red_indexing_all_on (
  input  big_index_turn,
  input  W3,
  input  W2,
  input  H3,
  input  H2,
  output index_turn
);

  wire not_3_out, not_4_out, or_1_out;

  // NOT_Gate not_1 has open pins: in=W3, out=open
  // NOT_Gate not_2 has open pins: in=W2, out=open
  not not_3 (not_3_out, H3);
  not not_4 (not_4_out, H2);
  or or_1 (or_1_out, W3, W2, not_3_out, not_4_out);
  and and_1 (index_turn, big_index_turn, or_1_out);
endmodule

module red_indexing_type_2 (
  input  big_index_turn,
  input  W3,
  input  W2,
  input  H3,
  input  H2,
  output index_turn
);

  wire and_1_out, not_1_out, not_2_out;

  not not_1 (not_1_out, W3);
  not not_2 (not_2_out, W2);
  // NOT_Gate not_3 has open pins: in=H3, out=open
  // NOT_Gate not_4 has open pins: in=H2, out=open
  and and_1 (and_1_out, not_1_out, not_2_out, H3, H2);
  and and_2 (index_turn, big_index_turn, and_1_out);
endmodule

module kmap_type_2 (
  input  index_turn,
  input  W1,
  input  W0,
  input  H1,
  input  H0,
  output on_color,
  output off_color
);

  wire and_1_out, not_3_out, not_4_out, not_5_out, or_1_out;

  // NOT_Gate not_1 has open pins: in=W1, out=open
  // NOT_Gate not_2 has open pins: in=W0, out=open
  not not_3 (not_3_out, H1);
  not not_4 (not_4_out, H0);
  and and_1 (and_1_out, W0, not_4_out);
  or or_1 (or_1_out, not_3_out, W1, and_1_out);
  not not_5 (not_5_out, or_1_out);
  and and_2 (on_color, index_turn, or_1_out);
  and and_3 (off_color, index_turn, not_5_out);
endmodule

module big_subsystem_1100 (
  input  W5,
  input  W4,
  input  H5,
  input  H4,
  input  W3,
  input  W2,
  input  H3,
  input  H2,
  input  W1,
  input  W0,
  input  H1,
  input  H0,
  output x5,
  output x4
);

  wire and_1_out, not_3_out, not_4_out, RED_IDX_ALL_ON_index_turn, RED_IDX_TYPE_2_index_turn,
       TYPE_2_off_color, TYPE_2_on_color;

  // NOT_Gate not_1 has open pins: in=W5, out=open
  // NOT_Gate not_2 has open pins: in=W4, out=open
  not not_3 (not_3_out, H5);
  not not_4 (not_4_out, H4);
  // NOT_Gate not_5 has open pins: in=W3, out=open
  // NOT_Gate not_6 has open pins: in=W2, out=open
  // NOT_Gate not_7 has open pins: in=H3, out=open
  // NOT_Gate not_8 has open pins: in=H2, out=open
  // NOT_Gate not_9 has open pins: in=W1, out=open
  // NOT_Gate not_10 has open pins: in=W0, out=open
  // NOT_Gate not_11 has open pins: in=H1, out=open
  // NOT_Gate not_12 has open pins: in=H0, out=open
  and and_1 (and_1_out, W5, W4, not_3_out, not_4_out);
  red_indexing_all_on RED_IDX_ALL_ON (
    .big_index_turn(and_1_out), .W3(W3), .W2(W2), .H3(H3), .H2(H2), .index_turn(RED_IDX_ALL_ON_index_turn));
  red_indexing_type_2 RED_IDX_TYPE_2 (
    .big_index_turn(and_1_out), .W3(W3), .W2(W2), .H3(H3), .H2(H2), .index_turn(RED_IDX_TYPE_2_index_turn));
  kmap_type_2 TYPE_2 (
    .index_turn(RED_IDX_TYPE_2_index_turn), .W1(W1), .W0(W0), .H1(H1), .H0(H0), .on_color(TYPE_2_on_color),
    .off_color(TYPE_2_off_color));
  or or_1 (x5, RED_IDX_ALL_ON_index_turn, TYPE_2_on_color);
  buf or_2 (x4, TYPE_2_off_color);  // OR_Gate
endmodule
