// Logisim project big_subsystem_1111.circ as structural Verilog
module green_indexing_type_4 (
  input  big_index_turn,
  input  W3,
  input  W2,
  input  H3,
  input  H2,
  output index_turn
);

  wire and_1_out, not_3_out, not_4_out;

  // NOT_Gate not_1 has open pins: in=W3, out=open
  // NOT_Gate not_2 has open pins: in=W2, out=open
  not not_3 (not_3_out, H3);
  not not_4 (not_4_out, H2);
  and and_1 (and_1_out, W3, W2, not_3_out, not_4_out);
  and and_2 (index_turn, big_index_turn, and_1_out);
endmodule

module green_indexing_type_11 (
  input  big_index_turn,
  input  W3,
  input  W2,
  input  H3,
  input  H2,
  output index_turn
);

  wire and_1_out, and_2_out, not_2_out, not_3_out, not_4_out, or_1_out;

  // NOT_Gate not_1 has open pins: in=W3, out=open
  not not_2 (not_2_out, W2);
  not not_3 (not_3_out, H3);
  not not_4 (not_4_out, H2);
  and and_1 (and_1_out, W3, not_2_out, not_3_out, not_4_out);
  and and_2 (and_2_out, W3, W2, not_3_out, H2);
  or or_1 (or_1_out, and_1_out, and_2_out);
  and and_3 (index_turn, big_index_turn, or_1_out);
endmodule

module blue_indexing_all_on (
  input  big_index_turn,
  input  W3,
  input  W2,
  input  H3,
  input  H2,
  output index_turn
);

  wire and_1_out, and_2_out, and_3_out, and_4_out, not_1_out, not_2_out, not_3_out, or_1_out;

  not not_1 (not_1_out, W3);
  not not_2 (not_2_out, W2);
  not not_3 (not_3_out, H3);
  // NOT_Gate not_4 has open pins: in=H2, out=open
  and and_1 (and_1_out, not_1_out, not_3_out);
  and and_2 (and_2_out, not_1_out, W2);
  and and_3 (and_3_out, W3, H3);
  and and_4 (and_4_out, W3, not_2_out, H2);
  or or_1 (or_1_out, and_1_out, and_2_out, and_3_out, and_4_out);
  and and_5 (index_turn, big_index_turn, or_1_out);
endmodule

module blue_indexing_type_4 (
  input  big_index_turn,
  input  W3,
  input  W2,
  input  H3,
  input  H2,
  output index_turn
);

  wire and_1_out, not_1_out, not_2_out, not_4_out;

  not not_1 (not_1_out, W3);
  not not_2 (not_2_out, W2);
  // NOT_Gate not_3 has open pins: in=H3, out=open
  not not_4 (not_4_out, H2);
  and and_1 (and_1_out, not_1_out, not_2_out, H3, not_4_out);
  and and_2 (index_turn, big_index_turn, and_1_out);
endmodule

module blue_indexing_type_14 (
  input  big_index_turn,
  input  W3,
  input  W2,
  input  H3,
  input  H2,
  output index_turn
);

  wire and_1_out, not_1_out, not_2_out;

  not not_1 (not_1_out, W3);
  not not_2 (not_2_out, W2);
  // NOT_Gate not_3 has open pins: in=H3, out=open
  // NOT_Gate not_4 has open pins: in=H2, out=open
  and and_1 (and_1_out, not_1_out, not_2_out, H3, H2);
  and and_2 (index_turn, big_index_turn, and_1_out);
endmodule

module kmap_type_4 (
  input  index_turn,
  input  W1,
  input  W0,
  input  H1,
  input  H0,
  output on_color,
  output off_color
);

  wire not_3_out, not_4_out, not_5_out, or_1_out;

  // NOT_Gate not_1 has open pins: in=W1, out=open
  // NOT_Gate not_2 has open pins: in=W0, out=open
  not not_3 (not_3_out, H1);
  not not_4 (not_4_out, H0);
  or or_1 (or_1_out, W1, W0, not_3_out, not_4_out);
  not not_5 (not_5_out, or_1_out);
  and and_1 (on_color, index_turn, or_1_out);
  and and_2 (off_color, index_turn, not_5_out);
endmodule

module kmap_type_11 (
  input  index_turn,
  input  W1,
  input  W0,
  input  H1,
  input  H0,
  output on_color,
  output off_color
);

  wire and_1_out, and_2_out, not_3_out, not_4_out, not_5_out, or_1_out;

  // NOT_Gate not_1 has open pins: in=W1, out=open
  // NOT_Gate not_2 has open pins: in=W0, out=open
  not not_3 (not_3_out, H1);
  not not_4 (not_4_out, H0);
  and and_1 (and_1_out, W1, W0, not_3_out);
  or or_1 (or_1_out, and_1_out, and_2_out);
  and and_2 (and_2_out, W1, not_3_out, not_4_out);
  not not_5 (not_5_out, or_1_out);
  and and_3 (on_color, index_turn, or_1_out);
  and and_4 (off_color, index_turn, not_5_out);
endmodule

module kmap_type_14 (
  input  index_turn,
  input  W1,
  input  W0,
  input  H1,
  input  H0,
  output on_color,
  output off_color
);

  wire and_1_out, and_2_out, not_3_out, not_4_out, not_5_out, or_1_out;

  // NOT_Gate not_1 has open pins: in=W1, out=open
  // NOT_Gate not_2 has open pins: in=W0, out=open
  not not_3 (not_3_out, H1);
  not not_4 (not_4_out, H0);
  and and_1 (and_1_out, W1, not_3_out);
  or or_1 (or_1_out, and_1_out, and_2_out);
  and and_2 (and_2_out, W1, W0, H1, not_4_out);
  not not_5 (not_5_out, or_1_out);
  and and_3 (on_color, index_turn, or_1_out);
  and and_4 (off_color, index_turn, not_5_out);
endmodule

module big_subsystem_1111 (
  input  W5,
  input  W4,
  input  H5,
  input  H4,
  input  W3,
  input  W2,
  input  H3,
  input  H2,
  input  W1,
  input  W0,
  input  H1,
  input  H0,
  output x3,
  output x2,
  output x1
);

  wire and_1_out, BLU_IDX_ALL_ON_index_turn, BLU_IDX_TYPE_4_index_turn, BLU_IDX_TYPE_14_index_turn,
       GRE_IDX_TYPE_4_index_turn, GRE_IDX_TYPE_11_index_turn, TYPE_4_2_off_color, TYPE_4_2_on_color,
       TYPE_4_off_color, TYPE_4_on_color, TYPE_11_off_color, TYPE_11_on_color, TYPE_14_off_color,
       TYPE_14_on_color;

  // NOT_Gate not_1 has open pins: in=W5, out=open
  // NOT_Gate not_2 has open pins: in=W4, out=open
  // NOT_Gate not_3 has open pins: in=H5, out=open
  // NOT_Gate not_4 has open pins: in=H4, out=open
  // NOT_Gate not_5 has open pins: in=W3, out=open
  // NOT_Gate not_6 has open pins: in=W2, out=open
  // NOT_Gate not_7 has open pins: in=H3, out=open
  // NOT_Gate not_8 has open pins: in=H2, out=open
  // NOT_Gate not_9 has open pins: in=W1, out=open
  // NOT_Gate not_10 has open pins: in=W0, out=open
  // NOT_Gate not_11 has open pins: in=H1, out=open
  // NOT_Gate not_12 has open pins: in=H0, out=open
  and and_1 (and_1_out, W5, W4, H5, H4);
  blue_indexing_all_on BLU_IDX_ALL_ON (
    .big_index_turn(and_1_out), .W3(W3), .W2(W2), .H3(H3), .H2(H2), .index_turn(BLU_IDX_ALL_ON_index_turn));
  green_indexing_type_4 GRE_IDX_TYPE_4 (
    .big_index_turn(and_1_out), .W3(W3), .W2(W2), .H3(H3), .H2(H2), .index_turn(GRE_IDX_TYPE_4_index_turn));
  green_indexing_type_11 GRE_IDX_TYPE_11 (
    .big_index_turn(and_1_out), .W3(W3), .W2(W2), .H3(H3), .H2(H2), .index_turn(GRE_IDX_TYPE_11_index_turn));
  blue_indexing_type_4 BLU_IDX_TYPE_4 (
    .big_index_turn(and_1_out), .W3(W3), .W2(W2), .H3(H3), .H2(H2), .index_turn(BLU_IDX_TYPE_4_index_turn));
  blue_indexing_type_14 BLU_IDX_TYPE_14 (
    .big_index_turn(and_1_out), .W3(W3), .W2(W2), .H3(H3), .H2(H2), .index_turn(BLU_IDX_TYPE_14_index_turn));
  kmap_type_4 TYPE_4 (
    .index_turn(GRE_IDX_TYPE_4_index_turn), .W1(W1), .W0(W0), .H1(H1), .H0(H0), .on_color(TYPE_4_on_color),
    .off_color(TYPE_4_off_color));
  kmap_type_11 TYPE_11 (
    .index_turn(GRE_IDX_TYPE_11_index_turn), .W1(W1), .W0(W0), .H1(H1), .H0(H0), .on_color(TYPE_11_on_color),
    .off_color(TYPE_11_off_color));
  kmap_type_4 TYPE_4_2 (
    .index_turn(BLU_IDX_TYPE_4_index_turn), .W1(W1), .W0(W0), .H1(H1), .H0(H0), .on_color(TYPE_4_2_on_color),
    .off_color(TYPE_4_2_off_color));
  kmap_type_14 TYPE_14 (
    .index_turn(BLU_IDX_TYPE_14_index_turn), .W1(W1), .W0(W0), .H1(H1), .H0(H0), .on_color(TYPE_14_on_color),
    .off_color(TYPE_14_off_color));
  or or_1 (x3, TYPE_4_on_color, TYPE_11_on_color);
  or or_2 (x2, TYPE_4_off_color, TYPE_11_off_color, TYPE_4_2_on_color, TYPE_14_on_color, BLU_IDX_ALL_ON_index_turn);
  or or_3 (x1, TYPE_4_2_off_color, TYPE_14_off_color);
endmodule
