// Logisim project main.circ as structural Verilog: 3 circuits, main circuit main
// project_1_bmi
module main (
  input  W5,
  input  W4,
  input  W3,
  input  W2,
  input  W1,
  input  W0,
  input  H5,
  input  H4,
  input  H3,
  input  H2,
  input  H1,
  input  H0,
  output x1,
  output x2,
  output x3,
  output x4,
  output x5
);

  project_1_bmi project_1_bmi_1 (
    .W5(W5), .W4(W4), .W3(W3), .W2(W2), .W1(W1), .W0(W0), .H5(H5), .H4(H4), .H3(H3), .H2(H2), .H1(H1),
    .H0(H0), .x1(x1), .x2(x2), .x3(x3), .x4(x4), .x5(x5));

  // Notes on the sheet:
  //   Submitted by:
  //   Mislang, Gabriel
  //   Peralta, Juan Marco
  //   Underweight
  //   Batistil, Mansur Khalil
  //   Mislang, Ethan Renell Sebastian
  //   MSB
  //   Weight Inputs
  //   Normal
  //   LSB
  //   Overweight
  //   MSB
  //   Height Inputs
  //   Obese Class I
  //   LSB
  //   Obese Class II
endmodule

module project_1_bmi (
  input  W5,
  input  W4,
  input  W3,
  input  W2,
  input  W1,
  input  W0,
  input  H5,
  input  H4,
  input  H3,
  input  H2,
  input  H1,
  input  H0,
  output x1,
  output x2,
  output x3,
  output x4,
  output x5
);

  wire BS_0000_x1, BS_0000_x2, BS_0001_x1, BS_0010_x1, BS_0011_x1, BS_0100_x1, BS_0100_x2, BS_0100_x3,
       BS_0100_x4, BS_0101_x1, BS_0101_x2, BS_0101_x3, BS_0110_x1, BS_0110_x2, BS_0111_x1, BS_1000_x3,
       BS_1000_x4, BS_1000_x5, BS_1001_x2, BS_1001_x3, BS_1001_x4, BS_1010_x1, BS_1010_x2, BS_1010_x3,
       BS_1011_x1, BS_1011_x2, BS_1100_x4, BS_1100_x5, BS_1101_x3, BS_1101_x4, BS_1101_x5, BS_1110_x2,
       BS_1110_x3, BS_1110_x4, BS_1111_x1, BS_1111_x2, BS_1111_x3;

  big_subsystem_0000 BS_0000 (
    .W5(W5), .W4(W4), .H5(H5), .H4(H4), .W3(W3), .W2(W2), .H3(H3), .H2(H2), .W1(W1), .W0(W0), .H1(H1),
    .H0(H0), .x1(BS_0000_x1), .x2(BS_0000_x2));
  big_subsystem_0001 BS_0001 (
    .W5(W5), .W4(W4), .H5(H5), .H4(H4), .W3(W3), .W2(W2), .H3(H3), .H2(H2), .W1(W1), .W0(W0), .H1(H1),
    .H0(H0), .x1(BS_0001_x1));
  or or_1 (x1, BS_0000_x1, BS_0100_x1, BS_0110_x1, BS_1011_x1, BS_1010_x1, BS_0101_x1, BS_1111_x1, BS_0111_x1, BS_0011_x1, BS_0010_x1, BS_0001_x1);
  big_subsystem_0010 BS_0010 (
    .W5(W5), .W4(W4), .H5(H5), .H4(H4), .W3(W3), .W2(W2), .H3(H3), .H2(H2), .W1(W1), .W0(W0), .H1(H1),
    .H0(H0), .x1(BS_0010_x1));
  or or_2 (x2, BS_0000_x2, BS_1110_x2, BS_0100_x2, BS_1011_x2, BS_1010_x2, BS_1001_x2, BS_0101_x2, BS_0110_x2, BS_1111_x2);
  big_subsystem_0011 BS_0011 (
    .W5(W5), .W4(W4), .H5(H5), .H4(H4), .W3(W3), .W2(W2), .H3(H3), .H2(H2), .W1(W1), .W0(W0), .H1(H1),
    .H0(H0), .x1(BS_0011_x1));
  or or_3 (x3, BS_1010_x3, BS_1001_x3, BS_0101_x3, BS_1111_x3, BS_0100_x3, BS_1110_x3, BS_1101_x3, BS_1000_x3);
  big_subsystem_0100 BS_0100 (
    .W5(W5), .W4(W4), .H5(H5), .H4(H4), .W3(W3), .W2(W2), .H3(H3), .H2(H2), .W1(W1), .W0(W0), .H1(H1),
    .H0(H0), .x4(BS_0100_x4), .x3(BS_0100_x3), .x2(BS_0100_x2), .x1(BS_0100_x1));
  or or_4 (x4, BS_1001_x4, BS_0100_x4, BS_1110_x4, BS_1101_x4, BS_1100_x4, BS_1000_x4);
  big_subsystem_0101 BS_0101 (
    .W5(W5), .W4(W4), .H5(H5), .H4(H4), .W3(W3), .W2(W2), .H3(H3), .H2(H2), .W1(W1), .W0(W0), .H1(H1),
    .H0(H0), .x1(BS_0101_x1), .x2(BS_0101_x2), .x3(BS_0101_x3));
  or or_5 (x5, BS_1101_x5, BS_1100_x5, BS_1000_x5);
  big_subsystem_0110 BS_0110 (
    .W5(W5), .W4(W4), .H5(H5), .H4(H4), .W3(W3), .W2(W2), .H3(H3), .H2(H2), .W1(W1), .W0(W0), .H1(H1),
    .H0(H0), .x1(BS_0110_x1), .x2(BS_0110_x2));
  big_subsystem_0111 BS_0111 (
    .W5(W5), .W4(W4), .H5(H5), .H4(H4), .W3(W3), .W2(W2), .H3(H3), .H2(H2), .W1(W1), .W0(W0), .H1(H1),
    .H0(H0), .x1(BS_0111_x1));
  big_subsystem_1000 BS_1000 (
    .W5(W5), .W4(W4), .H5(H5), .H4(H4), .W3(W3), .W2(W2), .H3(H3), .H2(H2), .W1(W1), .W0(W0), .H1(H1),
    .H0(H0), .x5(BS_1000_x5), .x4(BS_1000_x4), .x3(BS_1000_x3));
  big_subsystem_1001 BS_1001 (
    .W5(W5), .W4(W4), .H5(H5), .H4(H4), .W3(W3), .W2(W2), .H3(H3), .H2(H2), .W1(W1), .W0(W0), .H1(H1),
    .H0(H0), .x4(BS_1001_x4), .x3(BS_1001_x3), .x2(BS_1001_x2));
  big_subsystem_1010 BS_1010 (
    .W5(W5), .W4(W4), .H5(H5), .H4(H4), .W3(W3), .W2(W2), .H3(H3), .H2(H2), .W1(W1), .W0(W0), .H1(H1),
    .H0(H0), .x1(BS_1010_x1), .x2(BS_1010_x2), .x3(BS_1010_x3));
  big_subsystem_1011 BS_1011 (
    .W5(W5), .W4(W4), .H5(H5), .H4(H4), .W3(W3), .W2(W2), .H3(H3), .H2(H2), .W1(W1), .W0(W0), .H1(H1),
    .H0(H0), .x1(BS_1011_x1), .x2(BS_1011_x2));
  big_subsystem_1100 BS_1100 (
    .W5(W5), .W4(W4), .H5(H5), .H4(H4), .W3(W3), .W2(W2), .H3(H3), .H2(H2), .W1(W1), .W0(W0), .H1(H1),
    .H0(H0), .x5(BS_1100_x5), .x4(BS_1100_x4));
  big_subsystem_1101 BS_1101 (
    .W5(W5), .W4(W4), .H5(H5), .H4(H4), .W3(W3), .W2(W2), .H3(H3), .H2(H2), .W1(W1), .W0(W0), .H1(H1),
    .H0(H0), .x5(BS_1101_x5), .x4(BS_1101_x4), .x3(BS_1101_x3));
  big_subsystem_1110 BS_1110 (
    .W5(W5), .W4(W4), .H5(H5), .H4(H4), .W3(W3), .W2(W2), .H3(H3), .H2(H2), .W1(W1), .W0(W0), .H1(H1),
    .H0(H0), .x4(BS_1110_x4), .x3(BS_1110_x3), .x2(BS_1110_x2));
  big_subsystem_1111 BS_1111 (
    .W5(W5), .W4(W4), .H5(H5), .H4(H4), .W3(W3), .W2(W2), .H3(H3), .H2(H2), .W1(W1), .W0(W0), .H1(H1),
    .H0(H0), .x3(BS_1111_x3), .x2(BS_1111_x2), .x1(BS_1111_x1));
endmodule

module main_demo (
  output x1,
  output x2,
  output x3,
  output x4,
  output x5
);

  wire clock_1_out;
  wire [11:0] counter_1_q;

  Counter #(.width(12), .max('hfff)) counter_1 (
    .Q(counter_1_q), .clk(clock_1_out), .clr(1'b0));  // open: load, D, count, carry
  Clock clock_1 (.out(clock_1_out));
  project_1_bmi project_1_bmi_1 (
    .W5(counter_1_q[11]), .W4(counter_1_q[10]), .W3(counter_1_q[9]), .W2(counter_1_q[8]),
    .W1(counter_1_q[7]), .W0(counter_1_q[6]), .H5(counter_1_q[5]), .H4(counter_1_q[4]), .H3(counter_1_q[3]),
    .H2(counter_1_q[2]), .H1(counter_1_q[1]), .H0(counter_1_q[0]), .x1(x1), .x2(x2), .x3(x3), .x4(x4), .x5(x5));

  // Notes on the sheet:
  //   Underweight
  //   MSB
  //   W4
  //   W5
  //   W3
  //   Weight Inputs
  //   W1
  //   W2
  //   Normal
  //   LSB
  //   W0
  //   MSB
  //   H5
  //   Overweight
  //   H4
  //   Height Inputs
  //   H3
  //   H2
  //   Obese Class I
  //   LSB
  //   H1
  //   H0
  //   Obese Class II
endmodule
